# Fritzing sketch Schemat_mikrokontrolera (saved by Fritzing 0.9.9b)
circuit board: 29.6761cm x 18.1283cm
breadboards: 2

parts:
  MH-ET_LIVE_ESP32_DEVKIT1 = MH-ET LIVE ESP32 DEVKIT 38 pins
  HC-SR04_Sensor_1 = HC-SR04 Ultrasonic Distance Sensor
  Water_Level_Sensor1 = Water Level Sensor
  YL-83_-_Control_Board1 = YL-83 Rain Sensor - Control Board
  YL-83_-_Detection_Board1 = YL-83 Rain Sensor - Detection Board

nets:
  N1: MH-ET_LIVE_ESP32_DEVKIT1.IO34, YL-83_-_Control_Board1.AO
  N2: MH-ET_LIVE_ESP32_DEVKIT1.IO35, Water_Level_Sensor1.SIG
  N3: MH-ET_LIVE_ESP32_DEVKIT1.GND#58, HC-SR04_Sensor_1.GND
  N4: MH-ET_LIVE_ESP32_DEVKIT1.IO13, Water_Level_Sensor1.VCC
  5V: MH-ET_LIVE_ESP32_DEVKIT1.5V, HC-SR04_Sensor_1.VCC
  GND: MH-ET_LIVE_ESP32_DEVKIT1.GND#64, Water_Level_Sensor1.GND, YL-83_-_Control_Board1.GND
  N5: MH-ET_LIVE_ESP32_DEVKIT1.IO18, HC-SR04_Sensor_1.TRIG
  N6: MH-ET_LIVE_ESP32_DEVKIT1.IO5, HC-SR04_Sensor_1.ECHO
  N7: MH-ET_LIVE_ESP32_DEVKIT1.IO4, YL-83_-_Control_Board1.VCC
  N8: YL-83_-_Control_Board1.POS, YL-83_-_Detection_Board1.POS
  N9: YL-83_-_Control_Board1.NEG, YL-83_-_Detection_Board1.NEG

custom parts:
  MH-ET LIVE ESP32 DEVKIT 38 pins: http://mh.nodebb.com/topic/2/mh-et-live-esp32-devkit
  HC-SR04 Ultrasonic Distance Sensor: The HC-SR04 is an ultrasonic distance sensor. It is capable of providing measurement for ranges of 2cm to 400cm. The module operates at 5V.
  Water Level Sensor: A water level sensor. This sensor operates at 3V to 5V. The Sig (signal) pin outputs an analogue signal that is in proportion to the amount of water in contact with the sensor.
  YL-83 Rain Sensor - Control Board: The YL-83 is a rain sensor that has more resistance when dry and less resistance when wet. The module runs at 5V.
  YL-83 Rain Sensor - Detection Board: The YL-83 is a rain sensor that has more resistance when dry and less resistance when wet. The module runs at 5V.
