# Fritzing sketch alltestschemat (saved by Fritzing 0.9.9b)
breadboards: 1

parts:
  Water_Level_Sensor1 = Water Level Sensor
  YL-83_-_Control_Board1 = YL-83 Rain Sensor - Control Board
  YL-83_-_Detection_Board1 = YL-83 Rain Sensor - Detection Board
  Part1 = Arduino Uno (Rev3) - ICSP
  HC-SR04_Sensor_1 = HC-SR04 Ultrasonic Distance Sensor

nets:
  N1: Water_Level_Sensor1.SIG, Part1.A5/SCL
  VCC: Water_Level_Sensor1.VCC, YL-83_-_Control_Board1.VCC, Part1.5V, HC-SR04_Sensor_1.VCC
  GND: Water_Level_Sensor1.GND, YL-83_-_Control_Board1.GND, Part1.GND, HC-SR04_Sensor_1.GND
  N2: YL-83_-_Control_Board1.AO, Part1.A0
  N3: YL-83_-_Control_Board1.POS, YL-83_-_Detection_Board1.POS
  N4: YL-83_-_Control_Board1.NEG, YL-83_-_Detection_Board1.NEG
  N5: Part1.D9_PWM, HC-SR04_Sensor_1.TRIG
  N6: Part1.D10_PWM/SS, HC-SR04_Sensor_1.ECHO

custom parts:
  Water Level Sensor: A water level sensor. This sensor operates at 3V to 5V. The Sig (signal) pin outputs an analogue signal that is in proportion to the amount of water in contact with the sensor.
  YL-83 Rain Sensor - Control Board: The YL-83 is a rain sensor that has more resistance when dry and less resistance when wet. The module runs at 5V.
  YL-83 Rain Sensor - Detection Board: The YL-83 is a rain sensor that has more resistance when dry and less resistance when wet. The module runs at 5V.
  HC-SR04 Ultrasonic Distance Sensor: The HC-SR04 is an ultrasonic distance sensor. It is capable of providing measurement for ranges of 2cm to 400cm. The module operates at 5V.
